# Fritzing sketch pcb (saved by Fritzing 0.9.10b)
breadboards: 1

parts:
  Raspberry_Pi_1 = Raspberry Pi 3 [part_number=RPI-3-V1.2]
  LED1 = LED - 5mm [color="Yellow (585nm)" current=0.030 package="5 mm [THT]"]  # not connected
  S1 = Pushbutton [package="[SMD]"]
  LED2 = LED - 5mm [color="Blue (525nm)" current=0.030 package="5 mm [THT]"]
  U1 = TMP36 [package=to-92]

nets:
  GND: Raspberry_Pi_1.GND, U1.GND
  3V3: Raspberry_Pi_1.3V3, U1.VCC
  N1: Raspberry_Pi_1.GIPO26, U1.VOUT
  N2: S1.Pin_1, S1.Pin_2, LED2.anode

notes:
  It might be advisable to add some resistors in the LED circuits to prevent them from burning out.
  Camera is currently missing because it is not in the library.
